// Digital circuit nlprg5.dig as structural Verilog
module nlprg5 (
  input  ck,
  input  rst,
  output [4:0] o
);

  wire and_1_out, and_2_out, nor_1_out, not_1_out, xnor_1_out, xnor_2_out, xor_1_out, xor_2_out, xor_3_out,
       xor_4_out;

  xnor xnor_1 (xnor_1_out, xor_3_out, o[2]);
  D_FF_AS d_ff_as_1 (.Set(1'b0), .D(xnor_1_out), .C(ck), .Clr(rst), .Q(o[0]));  // open: nQ
  xor xor_1 (xor_1_out, xor_4_out, o[0]);
  D_FF_AS d_ff_as_2 (.Set(1'b0), .D(xor_1_out), .C(ck), .Clr(rst), .Q(o[1]));  // open: nQ
  xnor xnor_2 (xnor_2_out, o[2], o[1]);
  and and_1 (and_1_out, o[0], and_2_out);
  xor xor_2 (xor_2_out, xnor_2_out, and_1_out);
  and and_2 (and_2_out, nor_1_out, not_1_out);
  D_FF_AS d_ff_as_3 (.Set(1'b0), .D(xor_2_out), .C(ck), .Clr(rst), .Q(o[2]));  // open: nQ
  xor xor_3 (xor_3_out, o[2], o[4]);
  not not_1 (not_1_out, o[2]);
  xor xor_4 (xor_4_out, o[3], o[4]);
  D_FF_AS d_ff_as_4 (.Set(1'b0), .D(o[2]), .C(ck), .Clr(rst), .Q(o[3]));  // open: nQ
  nor nor_1 (nor_1_out, o[4], o[3]);
  D_FF_AS d_ff_as_5 (.Set(1'b0), .D(o[3]), .C(ck), .Clr(rst), .Q(o[4]));  // open: nQ
endmodule
