// Digital circuit nlprg16.dig as structural Verilog
module nlprg16 (
  input  ck,
  input  rst,
  output [15:0] o
);

  wire and_1_out, and_2_out, and_3_out, and_4_out, and_5_out, and_6_out, and_7_out, and_8_out, and_9_out,
       nor_1_out, nor_2_out, nor_3_out, nor_4_out, nor_5_out, not_1_out, xnor_1_out, xnor_2_out, xor_1_out,
       xor_2_out, xor_3_out, xor_4_out, xor_5_out, xor_6_out, xor_7_out, xor_8_out, xor_9_out, xor_10_out;

  xnor xnor_1 (xnor_1_out, xor_10_out, o[5]);
  D_FF_AS d_ff_as_1 (.Set(1'b0), .D(xnor_1_out), .C(ck), .Clr(rst), .Q(o[0]));  // open: nQ
  xor xor_1 (xor_1_out, xor_9_out, o[0]);
  D_FF_AS d_ff_as_2 (.Set(1'b0), .D(xor_1_out), .C(ck), .Clr(rst), .Q(o[1]));  // open: nQ
  xor xor_2 (xor_2_out, xor_8_out, o[1]);
  and and_1 (and_1_out, o[1], o[0]);
  D_FF_AS d_ff_as_3 (.Set(1'b0), .D(xor_2_out), .C(ck), .Clr(rst), .Q(o[2]));  // open: nQ
  xor xor_3 (xor_3_out, xor_7_out, o[2]);
  D_FF_AS d_ff_as_4 (.Set(1'b0), .D(xor_3_out), .C(ck), .Clr(rst), .Q(o[3]));  // open: nQ
  xor xor_4 (xor_4_out, xor_6_out, o[3]);
  and and_2 (and_2_out, o[3], o[2]);
  D_FF_AS d_ff_as_5 (.Set(1'b0), .D(xor_4_out), .C(ck), .Clr(rst), .Q(o[4]));  // open: nQ
  and and_3 (and_3_out, and_2_out, and_1_out);
  xnor xnor_2 (xnor_2_out, o[7], o[4]);
  xor xor_5 (xor_5_out, xnor_2_out, and_4_out);
  and and_4 (and_4_out, and_3_out, and_5_out);
  and and_5 (and_5_out, and_6_out, not_1_out);
  and and_6 (and_6_out, and_7_out, nor_1_out);
  D_FF_AS d_ff_as_6 (.Set(1'b0), .D(xor_5_out), .C(ck), .Clr(rst), .Q(o[5]));  // open: nQ
  not not_1 (not_1_out, o[5]);
  xor xor_6 (xor_6_out, o[6], o[7]);
  D_FF_AS d_ff_as_7 (.Set(1'b0), .D(o[5]), .C(ck), .Clr(rst), .Q(o[6]));  // open: nQ
  nor nor_1 (nor_1_out, o[7], o[6]);
  and and_7 (and_7_out, and_9_out, and_8_out);
  D_FF_AS d_ff_as_8 (.Set(1'b0), .D(o[6]), .C(ck), .Clr(rst), .Q(o[7]));  // open: nQ
  and and_8 (and_8_out, nor_3_out, nor_2_out);
  xor xor_7 (xor_7_out, o[8], o[9]);
  D_FF_AS d_ff_as_9 (.Set(1'b0), .D(o[7]), .C(ck), .Clr(rst), .Q(o[8]));  // open: nQ
  nor nor_2 (nor_2_out, o[9], o[8]);
  D_FF_AS d_ff_as_10 (.Set(1'b0), .D(o[8]), .C(ck), .Clr(rst), .Q(o[9]));  // open: nQ
  xor xor_8 (xor_8_out, o[10], o[11]);
  D_FF_AS d_ff_as_11 (.Set(1'b0), .D(o[9]), .C(ck), .Clr(rst), .Q(o[10]));  // open: nQ
  nor nor_3 (nor_3_out, o[11], o[10]);
  D_FF_AS d_ff_as_12 (.Set(1'b0), .D(o[10]), .C(ck), .Clr(rst), .Q(o[11]));  // open: nQ
  and and_9 (and_9_out, nor_5_out, nor_4_out);
  xor xor_9 (xor_9_out, o[12], o[13]);
  D_FF_AS d_ff_as_13 (.Set(1'b0), .D(o[11]), .C(ck), .Clr(rst), .Q(o[12]));  // open: nQ
  nor nor_4 (nor_4_out, o[13], o[12]);
  D_FF_AS d_ff_as_14 (.Set(1'b0), .D(o[12]), .C(ck), .Clr(rst), .Q(o[13]));  // open: nQ
  xor xor_10 (xor_10_out, o[14], o[15]);
  D_FF_AS d_ff_as_15 (.Set(1'b0), .D(o[13]), .C(ck), .Clr(rst), .Q(o[14]));  // open: nQ
  nor nor_5 (nor_5_out, o[15], o[14]);
  D_FF_AS d_ff_as_16 (.Set(1'b0), .D(o[14]), .C(ck), .Clr(rst), .Q(o[15]));  // open: nQ
endmodule
