// Digital circuit nlprg3.dig as structural Verilog
module nlprg3 (
  input  ck,
  input  rst,
  output [2:0] o
);

  wire nor_1_out, xnor_1_out, xnor_2_out, xor_1_out, xor_2_out;

  xnor xnor_1 (xnor_1_out, xor_2_out, o[1]);
  D_FF_AS d_ff_as_1 (.Set(1'b0), .D(xnor_1_out), .C(ck), .Clr(rst), .Q(o[0]));  // open: nQ
  xnor xnor_2 (xnor_2_out, o[1], o[0]);
  xor xor_1 (xor_1_out, xnor_2_out, nor_1_out);
  D_FF_AS d_ff_as_2 (.Set(1'b0), .D(xor_1_out), .C(ck), .Clr(rst), .Q(o[1]));  // open: nQ
  xor xor_2 (xor_2_out, o[1], o[2]);
  nor nor_1 (nor_1_out, o[2], o[1]);
  D_FF_AS d_ff_as_3 (.Set(1'b0), .D(o[1]), .C(ck), .Clr(rst), .Q(o[2]));  // open: nQ
endmodule
