// Digital circuit nlprg4.dig as structural Verilog
module nlprg4 (
  input  ck,
  input  rst,
  output [3:0] o
);

  wire and_1_out, nor_1_out, not_1_out, xnor_1_out, xnor_2_out, xor_1_out, xor_2_out;

  xnor xnor_1 (xnor_1_out, xor_2_out, o[1]);
  D_FF_AS d_ff_as_1 (.Set(1'b0), .D(xnor_1_out), .C(ck), .Clr(rst), .Q(o[0]));  // open: nQ
  xnor xnor_2 (xnor_2_out, o[2], o[0]);
  xor xor_1 (xor_1_out, xnor_2_out, and_1_out);
  and and_1 (and_1_out, nor_1_out, not_1_out);
  D_FF_AS d_ff_as_2 (.Set(1'b0), .D(xor_1_out), .C(ck), .Clr(rst), .Q(o[1]));  // open: nQ
  xor xor_2 (xor_2_out, o[2], o[3]);
  not not_1 (not_1_out, o[1]);
  D_FF_AS d_ff_as_3 (.Set(1'b0), .D(o[1]), .C(ck), .Clr(rst), .Q(o[2]));  // open: nQ
  nor nor_1 (nor_1_out, o[3], o[2]);
  D_FF_AS d_ff_as_4 (.Set(1'b0), .D(o[2]), .C(ck), .Clr(rst), .Q(o[3]));  // open: nQ
endmodule
