// Digital circuit nlprg9.dig as structural Verilog
module nlprg9 (
  input  ck,
  input  rst,
  output [8:0] o
);

  wire and_1_out, and_2_out, and_3_out, and_4_out, nor_1_out, nor_2_out, nor_3_out, xnor_1_out, xnor_2_out,
       xor_1_out, xor_2_out, xor_3_out, xor_4_out, xor_5_out, xor_6_out;

  xnor xnor_1 (xnor_1_out, xor_6_out, o[3]);
  D_FF_AS d_ff_as_1 (.Set(1'b0), .D(xnor_1_out), .C(ck), .Clr(rst), .Q(o[0]));  // open: nQ
  xor xor_1 (xor_1_out, xor_5_out, o[0]);
  D_FF_AS d_ff_as_2 (.Set(1'b0), .D(xor_1_out), .C(ck), .Clr(rst), .Q(o[1]));  // open: nQ
  xor xor_2 (xor_2_out, xor_4_out, o[1]);
  D_FF_AS d_ff_as_3 (.Set(1'b0), .D(xor_2_out), .C(ck), .Clr(rst), .Q(o[2]));  // open: nQ
  and and_1 (and_1_out, o[1], o[0]);
  xnor xnor_2 (xnor_2_out, o[8], o[2]);
  and and_2 (and_2_out, and_1_out, and_3_out);
  xor xor_3 (xor_3_out, xnor_2_out, and_2_out);
  and and_3 (and_3_out, and_4_out, nor_1_out);
  D_FF_AS d_ff_as_4 (.Set(1'b0), .D(xor_3_out), .C(ck), .Clr(rst), .Q(o[3]));  // open: nQ
  xor xor_4 (xor_4_out, o[3], o[5]);
  nor nor_1 (nor_1_out, o[4], o[3]);
  and and_4 (and_4_out, nor_3_out, nor_2_out);
  xor xor_5 (xor_5_out, o[4], o[6]);
  D_FF_AS d_ff_as_5 (.Set(1'b0), .D(o[3]), .C(ck), .Clr(rst), .Q(o[4]));  // open: nQ
  xor xor_6 (xor_6_out, o[7], o[8]);
  D_FF_AS d_ff_as_6 (.Set(1'b0), .D(o[4]), .C(ck), .Clr(rst), .Q(o[5]));  // open: nQ
  nor nor_2 (nor_2_out, o[6], o[5]);
  D_FF_AS d_ff_as_7 (.Set(1'b0), .D(o[5]), .C(ck), .Clr(rst), .Q(o[6]));  // open: nQ
  D_FF_AS d_ff_as_8 (.Set(1'b0), .D(o[6]), .C(ck), .Clr(rst), .Q(o[7]));  // open: nQ
  nor nor_3 (nor_3_out, o[8], o[7]);
  D_FF_AS d_ff_as_9 (.Set(1'b0), .D(o[7]), .C(ck), .Clr(rst), .Q(o[8]));  // open: nQ
endmodule
